# Fritzing sketch pwmled (saved by Fritzing 0.9.3b)
breadboards: 1

parts:
  Raspberry_Pi_1 = Raspberry Pi 3 [part_number=RPI-3-V1.2]
  LED3 = RGB LED (com. cathode, rgb) [package="5 mm [THT]"]

nets:
  N1: Raspberry_Pi_1.GND, LED3.common_cathode
  N2: Raspberry_Pi_1.GIPO18, LED3.green_anode
