# Fritzing sketch pwm_musicbox (saved by Fritzing 0.9.3b)
breadboards: 1

parts:
  Raspberry_Pi3_B+ = Raspberry Pi B+
  J1 = Piezo Speaker

nets:
  N1: Raspberry_Pi3_B+.GPIO18, J1.pin2
  N2: Raspberry_Pi3_B+.GND, J1.pin1
