# Fritzing sketch 红外接收头连接图 (saved by Fritzing 0.9.3b)
breadboards: 1

parts:
  IR1 = TSOP312.., 314.. [package=THT]
  Raspberry_Pi_1 = Raspberry Pi 3 [part_number=RPI-3-V1.2]

nets:
  GND: IR1.GND, Raspberry_Pi_1.GND
  N1: IR1.Vs, Raspberry_Pi_1.3v3
  N2: IR1.Data, Raspberry_Pi_1.GPIO18
